# Fritzing sketch prox_sensor (saved by Fritzing 0.9.3b)
breadboards: 1

parts:
  Part1 = Arduino Uno (Rev3)
  LED1 = LED - 5mm [color="Green (560nm)" package="5 mm [THT]"]
  LED2 = LED - 5mm [color="Red (633nm)" package="5 mm [THT]"]
  LED3 = LED - 5mm [color="Green (560nm)" package="5 mm [THT]"]
  LED4 = LED - 5mm [color="Red (633nm)" package="5 mm [THT]"]
  LED5 = LED - 5mm [color="Yellow (595nm)" package="5 mm [THT]"]
  LED6 = LED - 5mm [color="Yellow (592nm)" package="5 mm [THT]"]
  R1 = Resistor [tolerance=±5% resistance=220 package=THT]
  R2 = Resistor [tolerance=±5% resistance=220 package=THT]
  R3 = Resistor [tolerance=±5% resistance=220 package=THT]
  R4 = Resistor [tolerance=±5% resistance=220 package=THT]
  R5 = Resistor [tolerance=±5% resistance=220 package=THT]
  R6 = Resistor [tolerance=±5% resistance=220 package=THT]
  Part2 = SRF05 Ultrasonic Rangefinder
  J1 = Piezo Speaker

nets:
  N1: Part1.D8, R4.Pin_1
  N2: Part1.D9_PWM, R5.Pin_1
  N3: Part1.D10_PWM/SS, R6.Pin_1
  N4: Part1.D11_PWM/MOSI, Part2.Echo
  N5: Part1.D12/MISO, Part2.Trig
  GND: Part1.GND, LED1.cathode, LED2.cathode, LED3.cathode, LED4.cathode, LED5.cathode, LED6.cathode, Part2.GND, J1.pin1
  N6: Part1.D4, J1.pin2
  N7: Part1.D5_PWM, R1.Pin_1
  N8: Part1.D6_PWM, R2.Pin_1
  N9: Part1.D7, R3.Pin_1
  5V: Part1.5V, Part2.VCC
  N10: LED1.anode, R6.Pin_0
  N11: LED2.anode, R2.Pin_0
  N12: LED3.anode, R5.Pin_0
  N13: LED4.anode, R1.Pin_0
  N14: LED5.anode, R4.Pin_0
  N15: LED6.anode, R3.Pin_0

// code stored in the sketch: back_sensor.ino
#include "SR04.h"
#include "pitches.h"

#define PIN_GREEN_1 13;
#define PIN_GREEN_2 12;
#define PIN_YELLOW_1 11;
#define PIN_YELLOW_2 10;
#define PIN_RED_1 9;
#define PIN_RED_2 8;

#define PIN_BEEP 7;

#define PIN_ECHO 4;
#define PIN_TRIG 3;

#define DISTANCE_GREEN_1 100;
#define DISTANCE_GREEN_2 80;
#define DISTANCE_YELLOW_1 60;
#define DISTANCE_YELLOW_2 40;
#define DISTANCE_RED_1 20;
#define DISTANCE_RED_2 10;

SR04 sr04 = SR04(ECHO_PIN,TRIG_PIN);

long distance;

void setup() {
	pinMode(PIN_GREEN_1, OUTPUT);
	pinMode(PIN_GREEN_2, OUTPUT);
	pinMode(PIN_YELLOW_1, OUTPUT);
	pinMode(PIN_YELLOW_2, OUTPUT);
	pinMode(PIN_RED_1, OUTPUT);
	pinMode(PIN_RED_2, OUTPUT);
	pinMode(PIN_BEEP, OUTPUT);
}

void loop() {
	distance = sr04.Distance();

	checkDistance(PIN_GREEN_1, distance, DISTANCE_GREEN_1);
	checkDistance(PIN_GREEN_2, distance, DISTANCE_GREEN_2);
	checkDistance(PIN_YELLOW_1, distance, DISTANCE_YELLOW_1);
	checkDistance(PIN_YELLOW_2, distance, DISTANCE_YELLOW_2);
	checkDistance(PIN_RED_1, distance, DISTANCE_RED_1);
	checkDistance(PIN_RED_2, distance, DISTANCE_RED_2);

	beep(distance);
}

void checkDistance(int pin, long currentDistance, long maxDistance) {
	if (currentDistance <= maxDistance) {
		digitalWrite(pin, HIGH);
	} else {
		digitalWrite(pin, LOW);
	}
}

void beep(long distance) {
  int times = DISTANCE_GREEN_1 / distance;
	int interval = distance / DISTANCE_GREEN_1;

	for (int i = 0; i < times; i++) {
		tone(PIN_BEEP, NOTE_F5, 100);
		if (times > 1) {
			delay(interval * 50);
		}
	}
}

// code stored in the sketch: hc_sr04.ino
/*
HC-SR04 for Arduino

Original project from http://www.swanrobotics.com

This project demonstrates the HC-SR
The distance presented in the code is in mm, but you can uncomment the line for distance in inches.
The schematics for this project can be found on http://www.swanrobotics.com

This example code is in the public domain.
*/

const int TriggerPin = 8;      //Trig pin
const int EchoPin = 9;         //Echo pin
long Duration = 0;

void setup(){
  pinMode(TriggerPin,OUTPUT);  // Trigger is an output pin
  pinMode(EchoPin,INPUT);      // Echo is an input pin
  Serial.begin(9600);          // Serial Output
}

void loop(){ 
  digitalWrite(TriggerPin, LOW);                   
  delayMicroseconds(2);
  digitalWrite(TriggerPin, HIGH);          // Trigger pin to HIGH
  delayMicroseconds(10);                   // 10us high 
  digitalWrite(TriggerPin, LOW);           // Trigger pin to HIGH
 
  Duration = pulseIn(EchoPin,HIGH);        // Waits for the echo pin to get high
                                           // returns the Duration in microseconds
  long Distance_mm = Distance(Duration);   // Use function to calculate the distance
 
  Serial.print("Distance = ");             // Output to serial
  Serial.print(Distance_mm);
  Serial.println(" mm");
 
  delay(1000);                             // Wait to do next measurement
}

long Distance(long time)
{
    // Calculates the Distance in mm
    // ((time)*(Speed of sound))/ toward and backward of object) * 10
   
    long DistanceCalc;                      // Calculation variable
    DistanceCalc = ((time /2.9) / 2);     // Actual calculation in mm
    //DistanceCalc = time / 74 / 2;         // Actual calculation in inches
    return DistanceCalc;                    // return calculated value
}
